// Digital circuit a.dig as structural Verilog
module a (
  input  X,
  input  Y,
  input  Z,
  output A
);

  wire and_1_out, and_2_out, not_1_out, not_2_out;

  not not_1 (not_1_out, X);
  not not_2 (not_2_out, Z);
  and and_1 (and_1_out, X, Z);
  and and_2 (and_2_out, not_2_out, not_1_out);
  or or_1 (A, and_1_out, Y, and_2_out);
endmodule
