// Digital circuit b.dig as structural Verilog
module b (
  input  X,
  input  Y,
  input  Z,
  output B
);

  wire and_1_out, and_2_out, not_1_out, not_2_out, not_3_out;

  not not_1 (not_1_out, X);
  not not_2 (not_2_out, Y);
  not not_3 (not_3_out, Z);
  and and_1 (and_1_out, not_2_out, not_3_out);
  and and_2 (and_2_out, Z, Y);
  or or_1 (B, not_1_out, and_1_out, and_2_out);
endmodule
