// Digital circuit e.dig as structural Verilog
module e (
  input  X,
  input  Y,
  input  Z,
  output E
);

  wire not_1_out, not_2_out, or_1_out;

  not not_1 (not_1_out, X);
  not not_2 (not_2_out, Z);
  or or_1 (or_1_out, not_1_out, Y);
  and and_1 (E, or_1_out, not_2_out);
endmodule
