// Digital circuit f.dig as structural Verilog
module f (
  input  X,
  input  Y,
  input  Z,
  output F
);

  wire and_1_out, and_2_out, and_3_out, not_1_out, not_2_out;

  not not_1 (not_1_out, Y);
  not not_2 (not_2_out, Z);
  and and_1 (and_1_out, X, not_1_out);
  and and_2 (and_2_out, X, not_2_out);
  and and_3 (and_3_out, not_1_out, not_2_out);
  or or_1 (F, and_1_out, and_2_out, and_3_out);
endmodule
