// Digital circuit final simulator.dig as structural Verilog
module final_simulator (
  input  in_1,
  input  in_2,
  input  in_3
);

  wire a_icin_devre_1_p4, b_icin_devre_1_p4, c_icin_devre_1_p4, d_icin_devre_1_p4, e_icin_devre_1_p4,
       f_icin_devre_1_p4, g_icin_devre_1_p4;

  // g_icin_devre g_icin_devre_1: pin names not known; wires that end beside it: in_1, in_2, in_3, g_icin_devre_1_p4
  // d_icin_devre d_icin_devre_1: pin names not known; wires that end beside it: in_1, in_2, in_3, d_icin_devre_1_p4
  // f_icin_devre f_icin_devre_1: pin names not known; wires that end beside it: in_1, in_2, in_3, f_icin_devre_1_p4
  // e_icin_devre e_icin_devre_1: pin names not known; wires that end beside it: in_1, in_2, in_3, e_icin_devre_1_p4
  // c_icin_devre c_icin_devre_1: pin names not known; wires that end beside it: in_1, in_2, in_3, c_icin_devre_1_p4
  // b_icin_devre b_icin_devre_1: pin names not known; wires that end beside it: in_1, in_2, in_3, b_icin_devre_1_p4
  // a_icin_devre a_icin_devre_1: pin names not known; wires that end beside it: in_1, in_2, in_3, a_icin_devre_1_p4
  Seven_Seg seven_seg_1 (
    .a(a_icin_devre_1_p4), .b(b_icin_devre_1_p4), .c(c_icin_devre_1_p4), .d(d_icin_devre_1_p4),
    .e(e_icin_devre_1_p4), .f(f_icin_devre_1_p4), .g(g_icin_devre_1_p4), .dp(1'b0));
endmodule
