// Digital circuit g.dig as structural Verilog
module g (
  input  X,
  input  Y,
  input  Z,
  output G
);

  wire and_1_out, and_2_out, and_3_out, not_1_out, not_2_out, not_3_out;

  not not_1 (not_1_out, X);
  not not_2 (not_2_out, Y);
  not not_3 (not_3_out, Z);
  and and_1 (and_1_out, X, not_2_out);
  and and_2 (and_2_out, not_1_out, Y);
  and and_3 (and_3_out, Y, not_3_out);
  or or_1 (G, and_1_out, and_2_out, and_3_out);
endmodule
