// Digital circuit hw3.1.dig as structural Verilog
module hw3_1 (
  input  a,
  input  b,
  input  c,
  output O0,
  output O1,
  output O2,
  output O3,
  output O4,
  output O5,
  output O6,
  output O7
);

  wire not_1_out;

  not not_1 (not_1_out, c);
  Demultiplexer #(.Selector_Bits(2)) demultiplexer_1 (
    .sel({b, a}), .in(not_1_out), .out_0(O0), .out_1(O1), .out_2(O2), .out_3(O3));
  Demultiplexer #(.Selector_Bits(2)) demultiplexer_2 (
    .sel({b, a}), .in(c), .out_0(O4), .out_1(O5), .out_2(O6), .out_3(O7));
endmodule
