// Digital circuit hw3.4.dig as structural Verilog
module hw3_4 (
  input  X,
  input  Y,
  input  Z,
  output SUM,
  output CARRY
);

  wire not_1_out;

  not not_1 (not_1_out, Z);
  Multiplexer #(.Selector_Bits(2)) multiplexer_1 (
    .sel({Y, X}), .in_0(Z), .in_1(not_1_out), .in_2(not_1_out), .in_3(Z), .out(SUM));
  Multiplexer #(.Selector_Bits(2)) multiplexer_2 (
    .sel({Y, X}), .in_0(1'b0), .in_1(Z), .in_2(Z), .in_3(1'b1), .out(CARRY));
endmodule
