// Digital circuit statemachine.dig as structural Verilog
module statemachine (
  input  A,
  input  B,
  input  CLK,
  output OUT
);

  wire and_1_out, and_2_out, and_3_out, and_4_out, d_ff_1_nq, d_ff_1_q, d_ff_2_nq, d_ff_2_q, not_1_out,
       not_2_out, or_1_out, or_2_out;

  not not_1 (not_1_out, A);
  not not_2 (not_2_out, B);
  and and_1 (and_1_out, A, B, d_ff_2_q);
  and and_2 (and_2_out, d_ff_1_q, A, not_2_out);
  and and_3 (and_3_out, not_1_out, not_2_out, d_ff_1_nq);
  and and_4 (and_4_out, B, A, d_ff_2_q);
  or or_1 (or_1_out, and_1_out, and_2_out);
  or or_2 (or_2_out, and_3_out, and_4_out);
  D_FF d_ff_1 (.D(or_1_out), .C(CLK), .Q(d_ff_1_q), .nQ(d_ff_1_nq));
  D_FF d_ff_2 (.D(or_2_out), .C(CLK), .Q(d_ff_2_q), .nQ(d_ff_2_nq));
  and and_5 (OUT, d_ff_1_q, not_2_out, d_ff_2_nq, not_1_out);

  // Notes on the sheet:
  //   CLK: Hz: 20
endmodule
