// Digital circuit lab1a.dig as structural Verilog
module lab1a (
  input  in_1,
  input  in_2,
  input  in_3,
  input  in_4,
  input  in_5,
  input  in_6
);

  wire [3:0] add_1_s, unsignedbcd6_1_p1, unsignedbcd6_1_p3, unsignedbcd_1_p1, unsignedbcd_1_p3,
       unsignedbcd_2_p2, unsignedbcd_2_p3;
  wire [4:0] add_2_c_o, add_3_s;
  wire [4:4] add_1_c_o;
  wire [5:5] add_3_c_o;

  Add #(.Bits(4)) add_1 (
    .a({in_4, in_5, in_6, 1'b0}), .b({1'b0, in_4, in_5, in_6}), .c_i(1'b0), .s(add_1_s), .c_o(add_1_c_o[4]));
  Add #(.Bits(4)) add_2 (
    .a({in_1, in_2, in_3, 1'b0}), .b({1'b0, in_1, in_2, in_3}), .c_i(1'b0), .s(add_2_c_o[3:0]),
    .c_o(add_2_c_o[4]));
  Seven_Seg_Hex seven_seg_hex_1 (.d(unsignedbcd_1_p1), .dp(1'b0));
  Seven_Seg_Hex seven_seg_hex_2 (.d(unsignedbcd_1_p3), .dp(1'b0));
  // unsignedBCD unsignedbcd_1: pin names not known; wires that end beside it: unsignedbcd_1_p1, {1'b0, in_1, in_2, in_3}, unsignedbcd_1_p3
  Seven_Seg_Hex seven_seg_hex_3 (.d(unsignedbcd_2_p2), .dp(1'b0));
  Seven_Seg_Hex seven_seg_hex_4 (.d(unsignedbcd_2_p3), .dp(1'b0));
  // unsignedBCD unsignedbcd_2: pin names not known; wires that end beside it: {1'b0, in_4, in_5, in_6}, unsignedbcd_2_p2, unsignedbcd_2_p3, {1'b0, in_4, in_5, in_6}
  Add #(.Bits(5)) add_3 (.a(add_2_c_o), .b({add_1_c_o[4], add_1_s}), .c_i(1'b0), .s(add_3_s), .c_o(add_3_c_o[5]));
  Seven_Seg_Hex seven_seg_hex_5 (.d(unsignedbcd6_1_p1), .dp(1'b0));
  Seven_Seg_Hex seven_seg_hex_6 (.d(unsignedbcd6_1_p3), .dp(1'b0));
  // unsignedBCD6 unsignedbcd6_1: pin names not known; wires that end beside it: unsignedbcd6_1_p1, {add_3_c_o[5], add_3_s}, unsignedbcd6_1_p3

  // Notes on the sheet:
  //   3x
  //   +
  //   =
endmodule
