// Digital circuit lab2 nida.dig as structural Verilog
module lab2_nida (
  input  A,
  input  B,
  input  C,
  input  D,
  output Y,
  output X,
  output W,
  output V
);

  wire and_1_out, and_2_out, and_3_out, and_4_out, and_5_out, and_6_out, and_7_out, and_8_out, and_9_out,
       not_1_out, not_2_out, not_3_out, not_4_out;

  not not_1 (not_1_out, A);
  not not_2 (not_2_out, B);
  not not_3 (not_3_out, C);
  not not_4 (not_4_out, D);
  and and_1 (and_1_out, A, not_2_out);
  and and_2 (and_2_out, A, not_3_out);
  and and_3 (and_3_out, A, not_4_out);
  and and_4 (and_4_out, not_1_out, B);
  and and_5 (and_5_out, A, not_2_out);
  and and_6 (and_6_out, not_2_out, C);
  and and_7 (and_7_out, B, not_3_out);
  and and_8 (and_8_out, not_3_out, D);
  and and_9 (and_9_out, C, not_4_out);
  or or_1 (Y, and_1_out, and_2_out, and_3_out);
  or or_2 (X, and_4_out, and_5_out);
  or or_3 (W, and_6_out, and_7_out);
  or or_4 (V, and_8_out, and_9_out);
  LED led_1 (.in(Y));
  LED led_2 (.in(X));
  LED led_3 (.in(W));
  LED led_4 (.in(V));
endmodule
