// Digital circuit cnt4.dig as structural Verilog
module cnt4 (
  input  CLK,
  input  RST,
  output [7:0] CNT
);

  wire and_1_out, and_2_out, and_3_out, and_4_out, and_5_out, and_6_out, and_7_out, and_8_out, and_9_out,
       and_10_out, and_11_out, and_12_out, d_ff_1_nq, d_ff_2_nq, d_ff_3_nq, d_ff_4_nq, d_ff_5_nq, d_ff_6_nq,
       d_ff_7_nq, d_ff_8_nq, multiplexer_1_out, multiplexer_2_out, multiplexer_3_out, multiplexer_4_out,
       multiplexer_5_out, multiplexer_6_out, nor_1_out, not_1_out, not_2_out;

  not not_1 (not_1_out, RST);
  and and_1 (and_1_out, d_ff_1_nq, not_1_out);
  and and_2 (and_2_out, multiplexer_1_out, not_1_out);
  and and_3 (and_3_out, multiplexer_2_out, not_1_out);
  and and_4 (and_4_out, multiplexer_3_out, not_1_out);
  D_FF d_ff_1 (.D(and_1_out), .C(CLK), .Q(CNT[0]), .nQ(d_ff_1_nq));
  D_FF d_ff_2 (.D(and_2_out), .C(CLK), .Q(CNT[1]), .nQ(d_ff_2_nq));
  D_FF d_ff_3 (.D(and_3_out), .C(CLK), .Q(CNT[2]), .nQ(d_ff_3_nq));
  D_FF d_ff_4 (.D(and_4_out), .C(CLK), .Q(CNT[3]), .nQ(d_ff_4_nq));
  Multiplexer multiplexer_1 (.sel(CNT[0]), .in_0(CNT[1]), .in_1(d_ff_2_nq), .out(multiplexer_1_out));
  Multiplexer multiplexer_2 (.sel(and_5_out), .in_0(CNT[2]), .in_1(d_ff_3_nq), .out(multiplexer_2_out));
  Multiplexer multiplexer_3 (.sel(and_6_out), .in_0(CNT[3]), .in_1(d_ff_4_nq), .out(multiplexer_3_out));
  and and_5 (and_5_out, CNT[0], CNT[1]);
  and and_6 (and_6_out, CNT[2], and_5_out);
  nor nor_1 (nor_1_out, CNT[0], CNT[1], CNT[2], CNT[3]);
  not not_2 (not_2_out, RST);
  and and_7 (and_7_out, d_ff_5_nq, not_2_out);
  and and_8 (and_8_out, multiplexer_4_out, not_2_out);
  and and_9 (and_9_out, multiplexer_5_out, not_2_out);
  and and_10 (and_10_out, multiplexer_6_out, not_2_out);
  D_FF d_ff_5 (.D(and_7_out), .C(nor_1_out), .Q(CNT[4]), .nQ(d_ff_5_nq));
  D_FF d_ff_6 (.D(and_8_out), .C(nor_1_out), .Q(CNT[5]), .nQ(d_ff_6_nq));
  D_FF d_ff_7 (.D(and_9_out), .C(nor_1_out), .Q(CNT[6]), .nQ(d_ff_7_nq));
  D_FF d_ff_8 (.D(and_10_out), .C(nor_1_out), .Q(CNT[7]), .nQ(d_ff_8_nq));
  Multiplexer multiplexer_4 (.sel(CNT[4]), .in_0(CNT[5]), .in_1(d_ff_6_nq), .out(multiplexer_4_out));
  Multiplexer multiplexer_5 (.sel(and_11_out), .in_0(CNT[6]), .in_1(d_ff_7_nq), .out(multiplexer_5_out));
  Multiplexer multiplexer_6 (.sel(and_12_out), .in_0(CNT[7]), .in_1(d_ff_8_nq), .out(multiplexer_6_out));
  and and_11 (and_11_out, CNT[4], CNT[5]);
  and and_12 (and_12_out, CNT[6], and_11_out);
endmodule
