// Digital circuit abs.dig as structural Verilog
module abs (
  input  [3:0] in,
  output sign,
  output [3:0] out
);

  wire [2:0] xor_2_out;
  wire [2:2] xor_1_out;

  xor xor_1 (xor_1_out[2], in[3], 1'b0);
  assign xor_2_out = in[2:0] ^ {3{xor_1_out[2]}};  // XOr xor_2, 3 bits wide
  Add #(.Bits(3)) add_1 (.a(xor_2_out), .b({2'b00, xor_1_out[2]}), .c_i(1'b0), .s(out[2:0]), .c_o(out[3]));

  assign sign = in[3];
endmodule
