// Digital circuit counter4test.dig as structural Verilog
module counter4test (
  input  clk
);

  wire button_1_out;
  wire [3:0] cnt4_1_cnt;

  Button button_1 (.out(button_1_out));
  cnt4 cnt4_1 (.CLK(clk), .RST(button_1_out), .CNT(cnt4_1_cnt));
  Seven_Seg_Hex seven_seg_hex_1 (.d(cnt4_1_cnt), .dp(1'b0));
endmodule
