// Digital circuit nida.dig as structural Verilog
module nida (
  input  RESET,
  input  _100_Hz
);

  wire and_1_out, and_2_out, BD_out, BU_out, cntdecud_1_p1, cntdecud_1_p2, cntdecud_1_p6, cntdecud_1_p7,
       d_ff_1_nq, d_ff_2_nq;
  wire [3:0] cntdecud_1_p5, cntdecud_2_p5;

  and and_1 (and_1_out, cntdecud_1_p7, cntdecud_1_p1);
  and and_2 (and_2_out, cntdecud_1_p2, cntdecud_1_p6);
  Button BU (.out(BU_out));
  Button BD (.out(BD_out));
  // cntDECud cntdecud_1: pin names not known; wires that end beside it: cntdecud_1_p1, cntdecud_1_p2, _100_Hz, RESET, cntdecud_1_p5, cntdecud_1_p6, cntdecud_1_p7
  // cntDECud cntdecud_2: pin names not known; wires that end beside it: and_1_out, and_2_out, _100_Hz, RESET, cntdecud_2_p5
  D_FF d_ff_1 (.D(BU_out), .C(_100_Hz), .nQ(d_ff_1_nq));  // open: Q
  and and_3 (cntdecud_1_p1, d_ff_1_nq, BU_out);
  D_FF d_ff_2 (.D(BD_out), .C(_100_Hz), .nQ(d_ff_2_nq));  // open: Q
  and and_4 (cntdecud_1_p2, d_ff_2_nq, BD_out);
  Seven_Seg_Hex seven_seg_hex_1 (.d(cntdecud_2_p5), .dp(1'b0));
  Seven_Seg_Hex seven_seg_hex_2 (.d(cntdecud_1_p5), .dp(1'b0));

  // Notes on the sheet:
  //   _100_Hz: Hz: 100
endmodule
