// Digital circuit nidalab.dig as structural Verilog
module nidalab (
  input  _4_Hz
);

  wire and_1_out, and_2_out, and_3_out, cntdecud_1_p4, cntdecud_1_p6, cntdecud_3_p6, nand_2_out, t_ff_1_q,
       t_ff_2_q, t_ff_3_q, t_ff_4_q, t_ff_5_q, t_ff_6_q;
  wire [3:0] cntdecud_1_p5, cntdecud_2_p5, cntdecud_3_p5, cntdecud_4_p5;

  T_FF t_ff_1 (.T(1'b1), .C(_4_Hz), .Q(t_ff_1_q));  // open: nQ
  T_FF t_ff_2 (.T(and_3_out), .C(_4_Hz), .Q(t_ff_2_q));  // open: nQ
  T_FF t_ff_3 (.T(t_ff_1_q), .C(_4_Hz), .Q(t_ff_3_q));  // open: nQ
  T_FF t_ff_4 (.T(t_ff_2_q), .C(_4_Hz), .Q(t_ff_4_q));  // open: nQ
  T_FF t_ff_5 (.T(t_ff_3_q), .C(_4_Hz), .Q(t_ff_5_q));  // open: nQ
  T_FF t_ff_6 (.T(t_ff_4_q), .C(_4_Hz), .Q(t_ff_6_q));  // open: nQ
  and and_1 (and_1_out, cntdecud_1_p6, t_ff_5_q);
  // cntDECud cntdecud_1: pin names not known; wires that end beside it: t_ff_5_q, 1'b0, _4_Hz, cntdecud_1_p4, cntdecud_1_p5, cntdecud_1_p6
  // cntDECud cntdecud_2: pin names not known; wires that end beside it: and_1_out, 1'b0, _4_Hz, cntdecud_1_p4, cntdecud_2_p5
  and and_2 (and_2_out, t_ff_6_q, cntdecud_3_p6);
  nand nand_1 (cntdecud_1_p4, cntdecud_2_p5[2], cntdecud_2_p5[1]);
  and and_3 (and_3_out, cntdecud_1_p5[3], cntdecud_1_p5[0], cntdecud_2_p5[2], cntdecud_2_p5[0]);
  nand nand_2 (nand_2_out, cntdecud_4_p5[2], cntdecud_4_p5[1]);
  // cntDECud cntdecud_3: pin names not known; wires that end beside it: t_ff_6_q, 1'b0, _4_Hz, nand_2_out, cntdecud_3_p5, cntdecud_3_p6
  // cntDECud cntdecud_4: pin names not known; wires that end beside it: and_2_out, 1'b0, _4_Hz, nand_2_out, cntdecud_4_p5
  Seven_Seg_Hex seven_seg_hex_1 (.d(cntdecud_4_p5), .dp(1'b0));
  Seven_Seg_Hex seven_seg_hex_2 (.d(cntdecud_3_p5), .dp(1'b0));
  Seven_Seg_Hex seven_seg_hex_3 (.d(cntdecud_2_p5), .dp(1'b0));
  Seven_Seg_Hex seven_seg_hex_4 (.d(cntdecud_1_p5), .dp(1'b0));

  // Notes on the sheet:
  //   _4_Hz: Hz: 4
endmodule
